// Logisim project cpu.circ as structural Verilog: 3 circuits, main circuit cpu
module cpu (
  input  clk,
  input  ram_end,
  input  [31:0] ram_data,
  output [31:0] ram_read_addr
);

  wire data_path_1_p11, data_path_1_p12, data_path_1_p13, data_path_1_p14, data_path_1_p15, data_path_1_p16,
       immediate, rw;
  wire [1:0] data_selector;
  wire [3:0] alu_selector;
  wire [4:0] register_d, register_s, register_t;
  wire [5:0] func_code, op_code;
  wire [25:0] jump;
  wire [31:0] constant, pc_next, ram;

  Register #(.width(32)) PC (.D(pc_next), .en(ram_end), .Q(ram_read_addr), .clk(clk));  // open: clr
  branch_control branch_control_1 (
    .PC_in(ram_read_addr), .jump(1'b0), .flag(1'b0), .offset({16{1'b0}}), .PC_out(pc_next));
  // instruction_decoder instruction_decoder_1: pin names not known; wires that end beside it: ram_data, op_code, register_s, register_t, register_d, func_code, constant, jump, alu_selector, immediate, data_selector, rw
  // data_path data_path_1: pin names not known; wires that end beside it: register_t, register_d, register_s, rw, constant, ram, ram_end, alu_selector, data_selector, immediate, data_path_1_p11, data_path_1_p12, data_path_1_p13, data_path_1_p14, data_path_1_p15, data_path_1_p16

  // Other names for the same wires on the sheet: end = ram_end; instruction[31:0] = ram_data;
  //   pc_current[31:0] = ram_read_addr
endmodule

module cpu_test (
);

  wire clock_1_out, clock_2_out, fake_ram_1_end;
  wire [31:0] cpu_1_ram_read_addr, fake_ram_1_data;

  Clock clock_1 (.out(clock_1_out));
  fake_ram fake_ram_1 (.clk(clock_1_out), .\end (fake_ram_1_end), .data(fake_ram_1_data));
  Clock clock_2 (.out(clock_2_out));
  cpu cpu_1 (
    .ram_end(fake_ram_1_end), .ram_data(fake_ram_1_data), .ram_read_addr(cpu_1_ram_read_addr),
    .clk(clock_2_out));
  // Probe on cpu_1_ram_read_addr
endmodule

module fake_ram (
  input  clk,
  output \end ,
  output [31:0] data
);

  wire [1:0] counter_1_q;

  // Probe on 32'h20000001
  Counter #(.width(2), .max('h3)) counter_1 (.Q(counter_1_q), .clk(clk));  // open: load, D, count, carry, clr
  Comparator #(.width(2)) comparator_1 (.a(counter_1_q), .b(2'b11), .eq(\end ));  // open: gt, lt

  assign data = 32'h20000001;

  // Notes on the sheet:
  //   addi r0 5
endmodule
